# Fritzing sketch AnalogIO (saved by Fritzing 0.9.2b)
breadboards: 1

parts:
  Part1 = Arduino Pro Mini v13
  LED1 = smd LED [color="Blue (505nm)" package="1206 [SMD]"]
  R1 = Resistor [tolerance=±5% resistance=200 package=THT]
  U1 = POT [package=pot_alpha_rv16af-20]  # not connected

nets:
  N1: Part1.GND, R1.Pin_0
  N2: Part1.D10_PWM/SS, LED1.anode
  N3: LED1.cathode, R1.Pin_1

notes:
  The potentiometer is 10K ohm.
  The resistor is 200 ohm.
