# Fritzing sketch ESP8266_Bare_Module (saved by Fritzing 0.9.3b)
breadboards: 1

parts:
  S1 = Pushbutton [package="[SMD]"]
  S2 = Pushbutton [package="[SMD]"]
  R1 = Resistor [tolerance=±5% resistance=10k package="1206 [SMD]"]
  U1 = ESP8266 WiFi Module [part_number=ESP8266]
  Part1 = Barometric Pressure Sensor - BMP180 Breakout (GY-68)
  Part2 = FTDI Basic Programmer
  LED1 = smd LED [color="Blue (470nm)" package="0805 [SMD]"]
  R2 = Resistor [tolerance=±5% resistance=220 package="1206 [SMD]"]
  C1 = Capacitor Polarized [package=cpol-radial-100uf-25v]

nets:
  N1: S1.Pin_1, S1.Pin_2, R1.Pin_0, U1.GPIO_0
  GND: S1.Pin_3, S1.Pin_4, S2.Pin_3, S2.Pin_4, U1.GND, U1.GPIO_15, Part1.GND, Part2.GND, R2.Pin_1, C1.-
  N2: S2.Pin_1, S2.Pin_2, U1.GPIO_16, U1.REST
  VCC: R1.Pin_1, U1.VCC, U1.CH_PD, Part1.VCC, Part2.POWER, LED1.cathode, C1.+
  N3: U1.RXD, Part2.TXO
  N4: U1.TXD, Part2.RXI
  N5: U1.GPIO_5, Part1.SDA
  N6: U1.GPIO_13, Part1.SCL
  N7: LED1.anode, R2.Pin_0

notes:
  Flash Enable
  Chip Reset
  Any 3.3V USB-UART
  BMP180
  ESP2866MOD-12E
  Top (Metal) View
  Remove Power LED for μA Deep Sleep
  Optional
  power cap.
  10K Pullup on Flash Enable
